# Fritzing sketch OledPCB (saved by Fritzing 0.9.3b)
circuit board: 6.4591cm x 8.40323cm
breadboards: 1

parts:
  Part1 = Arduino Nano (Rev3.0)
  Part2 = NRF24L01+ Breakout Board
  BAT2 = Battery Holders [package=battcom_20mm_pth]
  S2 = Toggle Switch [package=THT]
  R2 = Resistor [tolerance=±5% resistance=220 package=THT]
  J1 = male pin header, 4 pins [form="♂ (male)"]
  S3 = Pushbutton [package=THT]
  BAT1 = Battery Holders [package=battcom_20mm_pth]

nets:
  GND: Part1.GND, Part2.GND, S2.COM, R2.Pin_0, J1.pin2
  N1: Part1.D2, R2.Pin_1, S3.leg0
  N2: Part1.D10, Part2.CS
  N3: Part1.D11/MOSI, Part2.MOSI
  N4: Part1.D12/MISO, Part2.MISO
  N5: Part1.VIN, BAT1.+
  N6: Part1.5V, J1.pin1, S3.leg1
  N7: Part1.A5, J1.pin3
  N8: Part1.A4, J1.pin4
  3V3: Part1.3V3, Part2.VCC
  N9: Part1.D13/SCK, Part2.SCK
  N10: BAT2.+, BAT1.-
  N11: BAT2.-, S2.L2

notes:
  Double-check your OLED pins match below (and adjust as needed) as they can vary across manufacturers.
  Please make sure the nRF24L01 module is connected to 3.3v only. Any higher may damage it.
  We use two CR2032 (3v each) cells in series for 6v. Any 6v - 20v power supply may be substituted.
  Top
  5V
  GND
  Vin
